// Digital circuit control-unit.dig as structural Verilog
module control_unit (
  input  [6:0] opcode,
  input  [6:0] funct7,
  input  [2:0] funct3,
  output ALUSrc,
  output [1:0] IMMSrc,
  output [3:0] ALUOp,
  output RegWrite
);

  wire [5:4] comparator_1_eq;

  Comparator #(.Bits(7)) comparator_1 (.a(opcode), .b(7'b0110011), .eq(comparator_1_eq[5]));  // open: gt, lt
  Comparator #(.Bits(7)) comparator_2 (.a(opcode), .b(7'b0010011), .eq(comparator_1_eq[4]));  // open: gt, lt
  ROM #(.AddrBits(6), .Bits(8)) rom_1 (
    .A({comparator_1_eq, funct7[5], funct3}), .sel(1'b1), .D({RegWrite, ALUSrc, IMMSrc, ALUOp}));

  // Notes on the sheet:
  //   contents of rom_1 (hex, n*v repeats v):
  //   16*0,c2,0,c7,4*0,c0,c2,0,c7,4*0,c0,82,84,87,0,0,85,81,80,86,4*0,88
endmodule
